# Fritzing sketch nodemcu-mains (saved by Fritzing 0.9.4)

parts:
  U2 = ESP8266 NodeMCU LoLin module
  RHT1 = Humidity and Temperature Sensor RHT03

nets (from the breadboard view):
  N1: U2.connector6, RHT1.GND_2
  N2: U2.connector7, RHT1.Data-signal
  N3: U2.connector8, RHT1.Vcc
